// Logisim project circ2.circ as structural Verilog: 1 circuit, main circuit main
module main (
  input  A,
  input  B,
  input  C,
  input  D,
  output Q
);

  wire and_1_out, and_2_out, and_3_out, and_4_out, not_1_out, not_2_out;

  not not_1 (not_1_out, A);
  and and_1 (and_1_out, not_1_out, B);
  not not_2 (not_2_out, D);
  and and_2 (and_2_out, A, B);
  and and_3 (and_3_out, and_1_out, C);
  and and_4 (and_4_out, not_2_out, and_2_out);
  or or_1 (Q, and_3_out, and_4_out);
endmodule
